# Fritzing sketch RPiPower - copia (saved by Fritzing 0.9.3b)
circuit board: 9.39994cm x 7.51992cm
breadboards: 1

parts:
  Part2 = Adafruit PowerBoost 1000C with Terminal Block [part_number="Adafruit #2465"]
  IC1 = MCP3008 8-channel 10-bit ADC [part_number=MCP3008]
  S1 = Pushbutton [package="[THT]"]
  LED1 = smd LED [color="Red (633nm)" package="0603 [SMD]"]
  LED2 = smd LED [color="Green (560nm)" package="0603 [SMD]"]
  Raspberry_Pi_1 = Raspberry Pi 3 [part_number=RPI-3-V1.2]
  D1 = Rectifier Diode [part_number=1N4001 package="300 mil [THT]"]
  D2 = Rectifier Diode [part_number=1N4001 package="300 mil [THT]"]
  R1 = Resistor [tolerance=±5% resistance=10k package=THT]
  C4 = Tantalum Capacitor [capacitance=0.1µF package="A 3216 [SMD, tantalum]"]
  D3 = Rectifier Diode [part_number=1N4001 package="300 mil [THT]"]
  R2 = Resistor [tolerance=±5% resistance=100k package=THT]
  R3 = Resistor [tolerance=±5% resistance=10k package=THT]
  C8 = Electrolytic Capacitor [capacitance=100µF package="200 mil [THT, electrolytic]"]
  R4 = Resistor [tolerance=±5% resistance=6.8k package=THT]
  R5 = Resistor [tolerance=±5% resistance=10k package=THT]
  R6 = Resistor [tolerance=±5% resistance=6.8k package=THT]
  R7 = Resistor [tolerance=±5% resistance=10k package=THT]
  R8 = Resistor [tolerance=±5% resistance=330 package=THT]
  R9 = Resistor [tolerance=±5% resistance=330 package=THT]
  C9 = Tantalum Capacitor [capacitance=0.1µF package="A 3216 [SMD, tantalum]"]

nets:
  N1: Part2.VBUS, R4.Pin_0
  N2: Part2.VLIPO, S1.Pin_1, S1.Pin_2, R6.Pin_0
  N3: Part2.ENABLE, D3.cathode, R2.Pin_0, R3.Pin_1, C8.+
  GND: Part2.GND, IC1.no_name_yet#9, IC1.no_name_yet#14, Raspberry_Pi_1.GND, C4.-, R2.Pin_1, C8.-, R5.Pin_1, R7.Pin_1, R8.Pin_1, R9.Pin_1, C9.-
  N4: IC1.no_name_yet#1, R6.Pin_1, R7.Pin_0
  N5: IC1.no_name_yet#2, R4.Pin_1, R5.Pin_0
  N6: IC1.no_name_yet#10, Raspberry_Pi_1.GIPO25
  N7: IC1.no_name_yet#11, Raspberry_Pi_1.GIPO24
  N8: IC1.no_name_yet#12, Raspberry_Pi_1.GIPO23
  N9: IC1.no_name_yet#13, Raspberry_Pi_1.GIPO18
  N10: IC1.no_name_yet#15, IC1.no_name_yet#16, Raspberry_Pi_1.3V3
  N11: S1.Pin_3, S1.Pin_4, D1.anode, D3.anode
  N12: LED1.cathode, R9.Pin_0
  N13: LED1.anode, Raspberry_Pi_1.GIPO21
  N14: LED2.cathode, R8.Pin_0
  N15: LED2.anode, Raspberry_Pi_1.GIPO20
  N16: Raspberry_Pi_1.GIPO26, R1.Pin_0, C4.+, C9.+
  N17: Raspberry_Pi_1.GIPO14, R3.Pin_0
  N18: D1.cathode, D2.anode
  N19: D2.cathode, R1.Pin_1

custom parts:
  Adafruit PowerBoost 1000C with Terminal Block: PowerBoost 1000C is the perfect power supply for your portable project! With a built-in load-sharing battery charger circuit, you'll be able to keep your power-hungry project running even while recharging the battery! This little DC/DC boost converter module can be powered by any 3.7V LiIon/LiPoly battery, and convert the battery output to 5.2V DC for running your 5V projects.
