# Fritzing sketch RPiPower (saved by Fritzing 0.9.3b)
circuit board: 9.39994cm x 7.51992cm
breadboards: 1

parts:
  Part2 = Adafruit PowerBoost 1000C with Terminal Block [part_number="Adafruit #2465"]
  S1 = Pushbutton [package="[THT]"]
  LED1 = smd LED [color="Red (633nm)" package="0603 [SMD]"]
  LED2 = smd LED [color="Green (560nm)" package="0603 [SMD]"]
  D1 = Rectifier Diode [part_number=1N4001 package="300 mil [THT]"]
  D2 = Rectifier Diode [part_number=1N4001 package="300 mil [THT]"]
  R1 = Resistor [tolerance=±5% resistance=10k package=THT]
  C4 = Tantalum Capacitor [capacitance=0.1µF package="A 3216 [SMD, tantalum]"]
  D3 = Rectifier Diode [part_number=1N4001 package="300 mil [THT]"]
  R2 = Resistor [tolerance=±5% resistance=100k package=THT]
  R3 = Resistor [tolerance=±5% resistance=10k package=THT]
  C8 = Electrolytic Capacitor [capacitance=100µF package="200 mil [THT, electrolytic]"]
  R4 = Resistor [tolerance=±5% resistance=6.8k package=THT]
  R5 = Resistor [tolerance=±5% resistance=10k package=THT]
  R6 = Resistor [tolerance=±5% resistance=6.8k package=THT]
  R7 = Resistor [tolerance=±5% resistance=10k package=THT]
  R8 = Resistor [tolerance=±5% resistance=330 package=THT]
  R9 = Resistor [tolerance=±5% resistance=330 package=THT]
  C9 = Tantalum Capacitor [capacitance=0.1µF package="A 3216 [SMD, tantalum]"]
  Part3 = RPi hat - blank [part_number=RPI-blank]
  JS1 = Generic Jumper Shunt
  JS2 = Generic Jumper Shunt
  IC1 = MCP3008 8-channel 10-bit ADC [part_number=MCP3008]

nets:
  N1: Part2.VBUS, R4.Pin_0
  N2: Part2.VLIPO, S1.Pin_1, S1.Pin_2, R6.Pin_0
  N3: Part2.ENABLE, D3.cathode, R2.Pin_0, R3.Pin_1, C8.+
  GND: Part2.GND, C4.-, R2.Pin_1, C8.-, R5.Pin_1, R7.Pin_1, R8.Pin_1, R9.Pin_1, C9.-, Part3.GND, JS2.pin1, JS2.pin2, IC1.no_name_yet#9, IC1.no_name_yet#14
  N4: Part2.5.0V, Part3.5.0V, JS1.pin1, JS1.pin2
  N5: S1.Pin_3, S1.Pin_4, D1.anode, D3.anode
  N6: LED1.cathode, R9.Pin_0
  N7: LED1.anode, Part3.GPIO21
  N8: LED2.cathode, R8.Pin_0
  N9: LED2.anode, Part3.GPIO20
  N10: D1.cathode, D2.anode
  N11: D2.cathode, R1.Pin_1
  N12: R1.Pin_0, C4.+, C9.+, Part3.GPIO26, Part3.GPIO27
  N13: R3.Pin_0, Part3.TXD
  N14: R4.Pin_1, R5.Pin_0, IC1.no_name_yet#2
  N15: R6.Pin_1, R7.Pin_0, IC1.no_name_yet#1
  N16: Part3.3.3V, IC1.no_name_yet#15, IC1.no_name_yet#16
  N17: Part3.GPIO23, IC1.no_name_yet#12
  N18: Part3.GPIO24, IC1.no_name_yet#11
  N19: Part3.GPIO25, IC1.no_name_yet#10
  N20: Part3.GPIO18, IC1.no_name_yet#13

custom parts:
  Adafruit PowerBoost 1000C with Terminal Block: PowerBoost 1000C is the perfect power supply for your portable project! With a built-in load-sharing battery charger circuit, you'll be able to keep your power-hungry project running even while recharging the battery! This little DC/DC boost converter module can be powered by any 3.7V LiIon/LiPoly battery, and convert the battery output to 5.2V DC for running your 5V projects.
