# Fritzing sketch RPiPowerV2 (saved by Fritzing 0.9.3b)
stripboards: 1

parts:
  Part1 = Adafruit PowerBoost 1000C [part_number="Adafruit #2465"]  # not connected
  S1 = Pushbutton [package="[THT]"]  # not connected
  D1 = Rectifier Diode [part_number=1N4001 package="300 mil [THT]"]  # not connected
  D2 = Rectifier Diode [part_number=1N4001 package="300 mil [THT]"]
  R1 = Resistor [tolerance=±5% resistance=220 package=THT]
  C1 = Ceramic Capacitor [capacitance=0.1µF package="100 mil [THT, multilayer]"]

nets:
  N1: D2.cathode, R1.Pin_1
  N2: R1.Pin_0, C1.0

custom parts:
  Adafruit PowerBoost 1000C: PowerBoost 1000C is the perfect power supply for your portable project! With a built-in load-sharing battery charger circuit, you'll be able to keep your power-hungry project running even while recharging the battery! This little DC/DC boost converter module can be powered by any 3.7V LiIon/LiPoly battery, and convert the battery output to 5.2V DC for running your 5V projects.
