# Fritzing sketch RPiPowerV3 (saved by Fritzing 0.9.3b)
stripboards: 1

parts:
  S1 = Pushbutton [package="[THT]"]
  D1 = Rectifier Diode [part_number=1N4001 package="300 mil [THT]"]
  D2 = Rectifier Diode [part_number=1N4001 package="300 mil [THT]"]
  R1 = Resistor [tolerance=±5% resistance=10k package=THT]
  C1 = Ceramic Capacitor [capacitance=0.1µF package="100 mil [THT, multilayer]"]
  D3 = Rectifier Diode [part_number=1N4001 package="300 mil [THT]"]
  R3 = Resistor [tolerance=±5% resistance=100k package=THT]

nets:
  N1: S1.Pin_1, S1.Pin_2
  N2: S1.Pin_3, S1.Pin_4, D1.anode, D3.anode
  N3: D1.cathode, D2.anode
  N4: D2.cathode, R1.Pin_1
  N5: R1.Pin_0, C1.1
  N6: C1.0, R3.Pin_1
  N7: D3.cathode, R3.Pin_0
